// Logisim project lojik ödevi en.circ as structural Verilog: 4 circuits, main circuit main
module main (
  input  Outside,
  input  Inside
);

  wire _0_kat_q, _1_kat_q, _1eCagirff2_q, _1eCagirff_q, _1egitff2_q, _1eGitff_q, _2_kat_q, _2yeCagirff2_q,
       _2yeCagirff_q, _2yeGitff2_q, _2yeGitff_q, \asansör_1_aşağı , \asansör_1_k1 , \asansör_1_k2 ,
       \asansör_1_kapı , \asansör_1_kz , \asansör_1_yukarı , \asansör_1_çb , CALL_to_1st_out,
       CALL_to_2nd_out, CALL_to_floor_out, Clock_out, decoder_1_out0, decoder_1_out1, decoder_2_out0,
       decoder_2_out1, GO_1st_out, Go_2nd_out, GO_floor_out, gosterge_1_a, gosterge_1_b, gosterge_1_c,
       gosterge_1_d, gosterge_1_e, gosterge_1_f, gosterge_1_g, gosterge_1_nokta, \katdüğmeleri_1_git0t ,
       \katdüğmeleri_1_git1t , \katdüğmeleri_1_git2t , \katdüğmeleri_1_çağı1t , \katdüğmeleri_1_çağır0t ,
       \katdüğmeleri_1_çağır2t , not_1_out, or_1_out, or_2_out, or_3_out, or_4_out, or_5_out, or_6_out,
       ZemineCagirff2_q, zemineCagirff_q, ZemineGitff2_q, zemineGitff_q;

  or or_1 (or_1_out, ZemineCagirff2_q, zemineCagirff_q);
  or or_2 (or_2_out, _2yeCagirff2_q, _2yeCagirff_q);
  or or_3 (or_3_out, _1egitff2_q, _1eGitff_q);
  Clock Clock (.out(Clock_out));
  D_Flip_Flop _0_kat (.clk(Clock_out), .D(\asansör_1_kz ), .Q(_0_kat_q));  // open: Qn, preset, en, reset
  D_Flip_Flop _1_kat (.clk(Clock_out), .D(\asansör_1_k1 ), .Q(_1_kat_q));  // open: Qn, preset, en, reset
  D_Flip_Flop _2_kat (.clk(Clock_out), .D(\asansör_1_k2 ), .Q(_2_kat_q));  // open: Qn, preset, en, reset
  D_Flip_Flop ZemineCagirff2 (
    .clk(Clock_out), .D(zemineCagirff_q), .Q(ZemineCagirff2_q));  // open: Qn, preset, en, reset
  D_Flip_Flop zemineCagirff (
    .clk(Clock_out), .D(\katdüğmeleri_1_çağır0t ), .Q(zemineCagirff_q));  // open: Qn, preset, en, reset
  D_Flip_Flop _2yeCagirff2 (.clk(Clock_out), .D(_2yeCagirff_q), .Q(_2yeCagirff2_q));  // open: Qn, preset, en, reset
  D_Flip_Flop _2yeCagirff (
    .clk(Clock_out), .D(\katdüğmeleri_1_çağır2t ), .Q(_2yeCagirff_q));  // open: Qn, preset, en, reset
  D_Flip_Flop _1egitff2 (.clk(Clock_out), .D(_1eGitff_q), .Q(_1egitff2_q));  // open: Qn, preset, en, reset
  D_Flip_Flop _1eGitff (.clk(Clock_out), .D(\katdüğmeleri_1_git1t ), .Q(_1eGitff_q));  // open: Qn, preset, en, reset
  D_Flip_Flop _1eCagirff2 (.clk(Clock_out), .D(_1eCagirff_q), .Q(_1eCagirff2_q));  // open: Qn, preset, en, reset
  or or_4 (or_4_out, _1eCagirff2_q, _1eCagirff_q);
  D_Flip_Flop _1eCagirff (
    .clk(Clock_out), .D(\katdüğmeleri_1_çağı1t ), .Q(_1eCagirff_q));  // open: Qn, preset, en, reset
  D_Flip_Flop ZemineGitff2 (.clk(Clock_out), .D(zemineGitff_q), .Q(ZemineGitff2_q));  // open: Qn, preset, en, reset
  or or_5 (or_5_out, ZemineGitff2_q, zemineGitff_q);
  D_Flip_Flop zemineGitff (
    .clk(Clock_out), .D(\katdüğmeleri_1_git0t ), .Q(zemineGitff_q));  // open: Qn, preset, en, reset
  D_Flip_Flop _2yeGitff2 (.clk(Clock_out), .D(_2yeGitff_q), .Q(_2yeGitff2_q));  // open: Qn, preset, en, reset
  or or_6 (or_6_out, _2yeGitff2_q, _2yeGitff2_q, _2yeGitff_q, _2yeGitff_q, _2yeGitff_q);
  D_Flip_Flop _2yeGitff (.clk(Clock_out), .D(\katdüğmeleri_1_git2t ), .Q(_2yeGitff_q));  // open: Qn, preset, en, reset
  \asansör  \asansör_1  (
    .zemint(_0_kat_q), .k1t(_1_kat_q), .k2t(_2_kat_q), .zemindenbasma(or_1_out), .k1basma(or_4_out),
    .k2basma(or_2_out), .kiz(or_5_out), .ki1(or_3_out), .ki2(or_6_out), .kz(\asansör_1_kz ),
    .k1(\asansör_1_k1 ), .k2(\asansör_1_k2 ), .\çb (\asansör_1_çb ), .\kapı (\asansör_1_kapı ),
    .\yukarı (\asansör_1_yukarı ), .\aşağı (\asansör_1_aşağı ));
  LED _0 (.in(\asansör_1_kz ));
  Decoder #(.enable("false")) decoder_1 (.out0(decoder_1_out0), .out1(decoder_1_out1), .sel(\asansör_1_kapı ));
  LED _2 (.in(\asansör_1_k2 ));
  LED _1 (.in(\asansör_1_k1 ));
  not not_1 (not_1_out, \asansör_1_çb );
  Decoder #(.enable("false")) decoder_2 (.out0(decoder_2_out0), .out1(decoder_2_out1), .sel(\asansör_1_çb ));
  gosterge gosterge_1 (
    .kat0(\asansör_1_kz ), .kat1(\asansör_1_k1 ), .kat2(\asansör_1_k2 ), .a(gosterge_1_a), .b(gosterge_1_b),
    .c(gosterge_1_c), .d(gosterge_1_d), .e(gosterge_1_e), .f(gosterge_1_f), .g(gosterge_1_g),
    .nokta(gosterge_1_nokta));
  _7_Segment_Display u_7_segment_display_1 (
    .g(gosterge_1_g), .f(gosterge_1_f), .a(gosterge_1_a), .b(gosterge_1_b), .e(gosterge_1_e),
    .d(gosterge_1_d), .c(gosterge_1_c), .dp(gosterge_1_nokta));
  LED Up (.in(\asansör_1_yukarı ));
  LED Down (.in(\asansör_1_aşağı ));
  LED Ready (.in(not_1_out));
  LED Door_Closed (.in(decoder_1_out1));
  Button CALL_to_2nd (.out(CALL_to_2nd_out));
  Button CALL_to_1st (.out(CALL_to_1st_out));
  Button CALL_to_floor (.out(CALL_to_floor_out));
  LED Door_Open (.in(decoder_1_out0));
  LED Busy (.in(decoder_2_out1));
  LED Usable (.in(decoder_2_out0));
  Button Go_2nd (.out(Go_2nd_out));
  Button GO_1st (.out(GO_1st_out));
  Button GO_floor (.out(GO_floor_out));
  \katdüğmeleri  \katdüğmeleri_1  (
    .git2(Go_2nd_out), .git1(GO_1st_out), .git0(GO_floor_out), .\çağır2 (CALL_to_2nd_out),
    .\çağır1 (CALL_to_1st_out), .\çağır0 (CALL_to_floor_out), .git2t(\katdüğmeleri_1_git2t ),
    .git1t(\katdüğmeleri_1_git1t ), .git0t(\katdüğmeleri_1_git0t ), .\çağır2t (\katdüğmeleri_1_çağır2t ),
    .\çağı1t (\katdüğmeleri_1_çağı1t ), .\çağır0t (\katdüğmeleri_1_çağır0t ));

  // Notes on the sheet:
  //   Flip Flop tetiklemesi
  //   Buton kullanıldıgı için çok uzun basılı tutmamak için koyulan Flip Floplar ve mesela 0. kattan 2. kata giderken 1. kat görünebilsin diye.
  //   Katları tutan Flip Floplar
  //   Decoderler 2 durumu tek bitle gösterebilmek için.
  //   Floor Display
  //   Başlangıç değeri 0. kat alındı.
endmodule

module gosterge (
  input  kat0,
  input  kat1,
  input  kat2,
  output a,
  output b,
  output c,
  output d,
  output e,
  output f,
  output g,
  output nokta
);

  wire and_1_out, and_2_out, and_3_out, and_4_out, and_5_out, and_6_out, and_7_out, and_8_out, and_9_out,
       and_10_out, and_11_out, not_1_out, not_2_out, not_3_out, not_4_out, not_5_out, not_6_out, not_7_out,
       not_8_out, not_9_out, not_10_out, not_11_out, not_12_out, not_13_out, not_14_out, not_15_out,
       not_16_out, not_17_out, not_18_out, not_19_out, not_20_out, not_21_out, not_22_out, not_23_out,
       not_24_out, not_25_out, not_26_out;

  not not_1 (not_1_out, kat0);
  not not_2 (not_2_out, kat1);
  not not_3 (not_3_out, kat1);
  not not_4 (not_4_out, kat2);
  not not_5 (not_5_out, kat0);
  not not_6 (not_6_out, kat1);
  not not_7 (not_7_out, kat0);
  not not_8 (not_8_out, kat2);
  not not_9 (not_9_out, kat1);
  not not_10 (not_10_out, kat2);
  not not_11 (not_11_out, kat0);
  not not_12 (not_12_out, kat2);
  not not_13 (not_13_out, kat1);
  not not_14 (not_14_out, kat2);
  not not_15 (not_15_out, kat0);
  not not_16 (not_16_out, kat1);
  not not_17 (not_17_out, kat1);
  not not_18 (not_18_out, kat2);
  not not_19 (not_19_out, kat0);
  not not_20 (not_20_out, kat1);
  not not_21 (not_21_out, kat1);
  not not_22 (not_22_out, kat2);
  not not_23 (not_23_out, kat1);
  not not_24 (not_24_out, kat2);
  not not_25 (not_25_out, kat0);
  not not_26 (not_26_out, kat1);
  and and_1 (and_1_out, not_1_out, not_2_out, kat2);
  and and_2 (and_2_out, kat0, not_3_out, not_4_out);
  and and_3 (and_3_out, not_5_out, not_6_out, kat2);
  and and_4 (and_4_out, not_7_out, kat1, not_8_out);
  and and_5 (and_5_out, kat0, not_9_out, not_10_out);
  and and_6 (and_6_out, not_11_out, kat1, not_12_out);
  and and_7 (and_7_out, kat0, not_13_out, not_14_out);
  and and_8 (and_8_out, not_15_out, not_16_out, kat2);
  and and_9 (and_9_out, kat0, not_17_out, not_18_out);
  and and_10 (and_10_out, not_19_out, not_20_out, kat2);
  and and_11 (and_11_out, kat0, not_21_out, not_22_out);
  and and_12 (f, kat0, not_23_out, not_24_out);
  and and_13 (g, not_25_out, not_26_out, kat2);
  or or_1 (a, and_1_out, and_2_out);
  or or_2 (b, and_3_out, and_4_out, and_5_out);
  or or_3 (c, and_6_out, and_7_out);
  or or_4 (d, and_8_out, and_9_out);
  or or_5 (e, and_10_out, and_11_out);

  assign nokta = 1'b1;
endmodule

module \asansör  (
  input  zemint,
  input  k1t,
  input  k2t,
  input  zemindenbasma,
  input  k1basma,
  input  k2basma,
  input  kiz,
  input  ki1,
  input  ki2,
  output kz,
  output k1,
  output k2,
  output \çb ,
  output \kapı ,
  output \yukarı ,
  output \aşağı 
);

  wire and_1_out, and_2_out, and_3_out, and_4_out, and_5_out, and_6_out, and_7_out, and_8_out, and_9_out,
       and_10_out, and_11_out, and_12_out, and_13_out, and_14_out, and_15_out, and_16_out, and_17_out,
       and_18_out, and_19_out, and_20_out, and_21_out, and_22_out, and_23_out, and_24_out, and_25_out,
       and_26_out, and_27_out, and_28_out, and_29_out, and_30_out, and_31_out, and_32_out, and_33_out,
       and_34_out, and_35_out, and_36_out, and_37_out, and_38_out, and_39_out, and_40_out, and_41_out,
       and_42_out, and_43_out, not_1_out, not_2_out, not_3_out, not_4_out, not_5_out, not_6_out, not_7_out,
       not_8_out, not_9_out, not_10_out, not_11_out, not_12_out, not_13_out, not_14_out, not_15_out,
       not_16_out, not_17_out, not_18_out, not_19_out, not_20_out, not_21_out, not_22_out, not_23_out,
       not_24_out, not_25_out, not_26_out, not_27_out, not_28_out, not_29_out, not_30_out, not_31_out,
       not_32_out, not_33_out, not_34_out, not_35_out, not_36_out, not_37_out, not_38_out, not_39_out,
       not_40_out, not_41_out, not_42_out;

  not not_1 (not_1_out, k1t);
  not not_2 (not_2_out, k2t);
  not not_3 (not_3_out, k1basma);
  not not_4 (not_4_out, k2basma);
  not not_5 (not_5_out, ki1);
  not not_6 (not_6_out, ki2);
  not not_7 (not_7_out, k2t);
  not not_8 (not_8_out, k2t);
  not not_9 (not_9_out, zemindenbasma);
  not not_10 (not_10_out, k2basma);
  not not_11 (not_11_out, kiz);
  not not_12 (not_12_out, ki2);
  not not_13 (not_13_out, zemint);
  not not_14 (not_14_out, zemint);
  not not_15 (not_15_out, zemindenbasma);
  not not_16 (not_16_out, k1basma);
  not not_17 (not_17_out, kiz);
  not not_18 (not_18_out, ki1);
  not not_19 (not_19_out, k2t);
  not not_20 (not_20_out, k1t);
  not not_21 (not_21_out, zemint);
  not not_22 (not_22_out, k2t);
  not not_23 (not_23_out, k1t);
  not not_24 (not_24_out, k2t);
  not not_25 (not_25_out, k1t);
  not not_26 (not_26_out, k1t);
  not not_27 (not_27_out, k2t);
  not not_28 (not_28_out, k1t);
  not not_29 (not_29_out, k2t);
  not not_30 (not_30_out, zemint);
  not not_31 (not_31_out, k2t);
  not not_32 (not_32_out, zemindenbasma);
  not not_33 (not_33_out, k1basma);
  not not_34 (not_34_out, kiz);
  not not_35 (not_35_out, ki1);
  not not_36 (not_36_out, k1t);
  not not_37 (not_37_out, k2t);
  not not_38 (not_38_out, k1t);
  not not_39 (not_39_out, k2t);
  not not_40 (not_40_out, zemint);
  not not_41 (not_41_out, k2basma);
  not not_42 (not_42_out, ki2);
  and and_1 (and_1_out, not_1_out, not_2_out, not_3_out, not_4_out, not_5_out, not_6_out);
  and and_2 (and_2_out, not_7_out, kiz);
  and and_3 (and_3_out, not_8_out, zemindenbasma);
  and and_4 (and_4_out, k2t, kiz);
  and and_5 (and_5_out, k2t, zemindenbasma);
  and and_6 (and_6_out, k1t, not_9_out, not_10_out, not_11_out, not_12_out);
  and and_7 (and_7_out, zemint, ki2);
  and and_8 (and_8_out, zemint, k2basma);
  and and_9 (and_9_out, not_13_out, ki2);
  and and_10 (and_10_out, not_14_out, k2basma);
  and and_11 (and_11_out, k2t, not_15_out, not_16_out, not_17_out, not_18_out);
  and and_12 (and_12_out, not_19_out, ki2);
  and and_13 (and_13_out, not_20_out, ki1);
  and and_14 (and_14_out, not_21_out, kiz);
  and and_15 (and_15_out, not_22_out, k2basma);
  and and_16 (and_16_out, not_23_out, k1basma);
  and and_17 (and_17_out, k2t, zemindenbasma);
  and and_18 (and_18_out, k1t, zemindenbasma);
  and and_19 (and_19_out, not_24_out, ki2);
  and and_20 (and_20_out, not_25_out, ki1);
  and and_21 (and_21_out, not_26_out, k1basma);
  and and_22 (and_22_out, k2t, kiz);
  and and_23 (and_23_out, k2t, zemindenbasma);
  and and_24 (and_24_out, k1t, kiz);
  and and_25 (and_25_out, k1t, k2basma);
  and and_26 (and_26_out, k1t, zemindenbasma);
  and and_27 (and_27_out, zemint, k2basma);
  and and_28 (and_28_out, not_27_out, ki2);
  and and_29 (and_29_out, not_28_out, not_29_out, ki1);
  and and_30 (and_30_out, not_30_out, not_31_out, not_32_out, not_33_out, k2basma, not_34_out, not_35_out);
  and and_31 (and_31_out, not_36_out, not_37_out, k2basma);
  and and_32 (and_32_out, not_38_out, not_39_out, k1basma);
  and and_33 (and_33_out, k2t, ki1);
  and and_34 (and_34_out, not_40_out, k2t, not_41_out, kiz, not_42_out);
  and and_35 (and_35_out, k2t, k1basma);
  and and_36 (and_36_out, k2t, zemindenbasma);
  and and_37 (and_37_out, k1t, kiz);
  and and_38 (and_38_out, k1t, k2basma, ki2);
  and and_39 (and_39_out, k1t, k2basma, ki1);
  and and_40 (and_40_out, k1t, k1basma, k2basma);
  and and_41 (and_41_out, k1t, zemindenbasma);
  and and_42 (and_42_out, k1t, k2t, k2basma);
  and and_43 (and_43_out, zemint, k1t, k2basma);
  or or_1 (kz, and_1_out, and_2_out, and_3_out);
  or or_2 (k1, ki1, k1basma, and_4_out, and_5_out, and_6_out, and_7_out, and_8_out);
  or or_3 (k2, and_9_out, and_10_out, and_11_out);
  or or_4 (\çb , and_12_out, and_13_out, and_14_out, and_15_out, and_16_out, and_17_out, and_18_out);
  or or_5 (\kapı , and_19_out, and_20_out, and_21_out, and_22_out, and_23_out, and_24_out, and_25_out, and_26_out, and_27_out);
  or or_6 (\yukarı , and_28_out, and_29_out, and_30_out, and_31_out, and_32_out);
  or or_7 (\aşağı , and_33_out, and_34_out, and_35_out, and_36_out, and_37_out, and_38_out, and_39_out, and_40_out, and_41_out, and_42_out, and_43_out);
endmodule

module \katdüğmeleri  (
  input  git2,
  input  git1,
  input  git0,
  input  \çağır2 ,
  input  \çağır1 ,
  input  \çağır0 ,
  output git2t,
  output git1t,
  output git0t,
  output \çağır2t ,
  output \çağı1t ,
  output \çağır0t 
);

  wire clock_1_out;

  Clock clock_1 (.out(clock_1_out));
  D_Flip_Flop git2ff (.Q(git2t), .preset(git2), .reset(clock_1_out));  // open: clk, D, Qn, en
  D_Flip_Flop git1ff (.Q(git1t), .preset(git1), .reset(clock_1_out));  // open: clk, D, Qn, en
  D_Flip_Flop git0ff (.Q(git0t), .preset(git0), .reset(clock_1_out));  // open: clk, D, Qn, en
  D_Flip_Flop \u_çağır2ff  (.Q(\çağır2t ), .preset(\çağır2 ), .reset(clock_1_out));  // open: clk, D, Qn, en
  D_Flip_Flop \u_çağır1ff  (.Q(\çağı1t ), .preset(\çağır1 ), .reset(clock_1_out));  // open: clk, D, Qn, en
  D_Flip_Flop \u_çağır0ff  (.Q(\çağır0t ), .preset(\çağır0 ), .reset(clock_1_out));  // open: clk, D, Qn, en
endmodule
